// Logisim project dcmp.circ as structural Verilog: 8 circuits, main circuit main
// MULTIPLIER
module main (
  input  in_1,
  input  in_2,
  input  in_3,
  input  in_4,
  input  in_5,
  input  in_6,
  input  in_7,
  input  in_8,
  input  in_9,
  input  in_10,
  input  in_11,
  input  in_12,
  input  in_13,
  input  in_14,
  input  in_15,
  input  in_16,
  input  [1:0] in_17
);

  wire A0, A1, A2, A3, adder_subtractor_1_sign, and_1_out, B0, B1, B2, B3, C0, C1, C2, C3, D0, D1, D2, D3,
       n7segdisplay_1_out_5, n7segdisplay_1_out_6, n7segdisplay_1_out_7, n7segdisplay_1_out_8,
       n7segdisplay_1_out_9, n7segdisplay_1_out_10, n7segdisplay_1_out_11, n7segdisplay_2_out_5,
       n7segdisplay_2_out_6, n7segdisplay_2_out_7, n7segdisplay_2_out_8, n7segdisplay_2_out_9,
       n7segdisplay_2_out_10, n7segdisplay_2_out_11, n7segdisplay_3_out_5, n7segdisplay_3_out_6,
       n7segdisplay_3_out_7, n7segdisplay_3_out_8, n7segdisplay_3_out_9, n7segdisplay_3_out_10,
       n7segdisplay_3_out_11, n7segdisplay_4_out_5, n7segdisplay_4_out_6, n7segdisplay_4_out_7,
       n7segdisplay_4_out_8, n7segdisplay_4_out_9, n7segdisplay_4_out_10, n7segdisplay_4_out_11, not_1_out;
  wire [7:0] adder_subtractor_1_s0;
  wire [15:0] divider_1_out_24, multiplier_1_out_23;

  Divider divider_1 (
    .in_1(in_9), .in_2(in_10), .in_3(in_11), .in_4(in_12), .in_5(in_13), .in_6(in_14), .in_7(in_15),
    .in_8(in_16), .in_9(in_1), .in_10(in_2), .in_11(in_3), .in_12(in_4), .in_13(in_5), .in_14(in_6),
    .in_15(in_7), .in_16(in_8), .out_17(divider_1_out_24[7]), .out_25(divider_1_out_24[15]),
    .out_18(divider_1_out_24[6]), .out_26(divider_1_out_24[14]), .out_19(divider_1_out_24[5]),
    .out_27(divider_1_out_24[13]), .out_20(divider_1_out_24[4]), .out_28(divider_1_out_24[12]),
    .out_21(divider_1_out_24[3]), .out_29(divider_1_out_24[11]), .out_22(divider_1_out_24[2]),
    .out_30(divider_1_out_24[10]), .out_23(divider_1_out_24[1]), .out_31(divider_1_out_24[9]),
    .out_24(divider_1_out_24[0]), .out_32(divider_1_out_24[8]));
  multiplier multiplier_1 (
    .in_1(in_1), .in_2(in_2), .in_3(in_3), .in_4(in_4), .in_5(in_5), .in_6(in_6), .in_7(in_7), .in_8(in_8),
    .in_9(in_9), .in_10(in_10), .in_11(in_11), .in_12(in_12), .in_13(in_13), .in_14(in_14), .in_15(in_15),
    .in_16(in_16), .out_24(multiplier_1_out_23[15]), .out_25(multiplier_1_out_23[14]),
    .out_26(multiplier_1_out_23[13]), .out_27(multiplier_1_out_23[12]), .out_28(multiplier_1_out_23[11]),
    .out_29(multiplier_1_out_23[10]), .out_30(multiplier_1_out_23[9]), .out_31(multiplier_1_out_23[8]),
    .out_32(multiplier_1_out_23[7]), .out_17(multiplier_1_out_23[6]), .out_18(multiplier_1_out_23[5]),
    .out_19(multiplier_1_out_23[4]), .out_20(multiplier_1_out_23[3]), .out_21(multiplier_1_out_23[2]),
    .out_22(multiplier_1_out_23[1]), .out_23(multiplier_1_out_23[0]));
  adder_subtractor adder_subtractor_1 (
    .A7(in_1), .A6(in_2), .A5(in_3), .A4(in_4), .A3(in_5), .A2(in_6), .A1(in_7), .A0(in_8), .B7(in_9),
    .B6(in_10), .B5(in_11), .B4(in_12), .B3(in_13), .B2(in_14), .B1(in_15), .B0(in_16), .M(in_17[0]),
    .S0(adder_subtractor_1_s0[0]), .S1(adder_subtractor_1_s0[1]), .S2(adder_subtractor_1_s0[2]),
    .S3(adder_subtractor_1_s0[3]), .S4(adder_subtractor_1_s0[4]), .S5(adder_subtractor_1_s0[5]),
    .S6(adder_subtractor_1_s0[6]), .S7(adder_subtractor_1_s0[7]), .Sign(adder_subtractor_1_sign));  // open: V
  not not_1 (not_1_out, adder_subtractor_1_sign);
  and and_1 (and_1_out, in_17[0], not_1_out);
  Multiplexer #(.select(2), .width(16), .enable("false")) multiplexer_1 (
    .in0({{8{1'b0}}, adder_subtractor_1_s0}), .in1({{8{1'b0}}, adder_subtractor_1_s0}),
    .in2(multiplier_1_out_23), .in3(divider_1_out_24),
    .out({D3, D2, D1, D0, C3, C2, C1, C0, B3, B2, B1, B0, A3, A2, A1, A0}), .sel(in_17));
  _7_Segment_Display u_7_segment_display_1 (.g(and_1_out));  // open: f, a, b, e, d, c, dp
  _7_Segment_Display u_7_segment_display_2 (
    .g(n7segdisplay_1_out_11), .f(n7segdisplay_1_out_9), .a(n7segdisplay_1_out_10), .b(n7segdisplay_1_out_5),
    .e(n7segdisplay_1_out_8), .d(n7segdisplay_1_out_7), .c(n7segdisplay_1_out_6));  // open: dp
  _7segdisplay u_7segdisplay_1 (
    .out_5(n7segdisplay_1_out_5), .out_6(n7segdisplay_1_out_6), .out_7(n7segdisplay_1_out_7),
    .out_8(n7segdisplay_1_out_8), .out_9(n7segdisplay_1_out_9), .out_10(n7segdisplay_1_out_10),
    .out_11(n7segdisplay_1_out_11), .A(D3), .B(D2), .C(D1), .D(D0));
  _7_Segment_Display u_7_segment_display_3 (
    .g(n7segdisplay_2_out_11), .f(n7segdisplay_2_out_9), .a(n7segdisplay_2_out_10), .b(n7segdisplay_2_out_5),
    .e(n7segdisplay_2_out_8), .d(n7segdisplay_2_out_7), .c(n7segdisplay_2_out_6));  // open: dp
  _7segdisplay u_7segdisplay_2 (
    .out_5(n7segdisplay_2_out_5), .out_6(n7segdisplay_2_out_6), .out_7(n7segdisplay_2_out_7),
    .out_8(n7segdisplay_2_out_8), .out_9(n7segdisplay_2_out_9), .out_10(n7segdisplay_2_out_10),
    .out_11(n7segdisplay_2_out_11), .A(C3), .B(C2), .C(C1), .D(C0));
  _7_Segment_Display u_7_segment_display_4 (
    .g(n7segdisplay_3_out_11), .f(n7segdisplay_3_out_9), .a(n7segdisplay_3_out_10), .b(n7segdisplay_3_out_5),
    .e(n7segdisplay_3_out_8), .d(n7segdisplay_3_out_7), .c(n7segdisplay_3_out_6));  // open: dp
  _7segdisplay u_7segdisplay_3 (
    .out_5(n7segdisplay_3_out_5), .out_6(n7segdisplay_3_out_6), .out_7(n7segdisplay_3_out_7),
    .out_8(n7segdisplay_3_out_8), .out_9(n7segdisplay_3_out_9), .out_10(n7segdisplay_3_out_10),
    .out_11(n7segdisplay_3_out_11), .A(B3), .B(B2), .C(B1), .D(B0));
  _7_Segment_Display u_7_segment_display_5 (
    .g(n7segdisplay_4_out_11), .f(n7segdisplay_4_out_9), .a(n7segdisplay_4_out_10), .b(n7segdisplay_4_out_5),
    .e(n7segdisplay_4_out_8), .d(n7segdisplay_4_out_7), .c(n7segdisplay_4_out_6));  // open: dp
  _7segdisplay u_7segdisplay_4 (
    .out_5(n7segdisplay_4_out_5), .out_6(n7segdisplay_4_out_6), .out_7(n7segdisplay_4_out_7),
    .out_8(n7segdisplay_4_out_8), .out_9(n7segdisplay_4_out_9), .out_10(n7segdisplay_4_out_10),
    .out_11(n7segdisplay_4_out_11), .A(A3), .B(A2), .C(A1), .D(A0));

  // Other names for the same wires on the sheet: AI0 = in_8; AI1 = in_7; AI2 = in_6; AI3 = in_5; AI4 = in_4;
  //   AI5 = in_3; AI6 = in_2; AI7 = in_1; BI0 = in_16; BI1 = in_15; BI2 = in_14; BI3 = in_13; BI4 = in_12;
  //   BI5 = in_11; BI6 = in_10; BI7 = in_9; C = in_17[0]; Ch[1:0] = in_17

  // Notes on the sheet:
  //   Put your choice:
  //   00- Addition
  //   01- Subtraction
  //   10- Multiplication
  //   11- Division
  //   ADDER/SUBTRACTOR
  //   MULTIPLIER
  //   DIVIDER
  //   NOTE: IN DIVISION FIRST TWO DISPLAYS ARE REMAINDER AND END TWO ARE QUOTIENTS.
  //   SIGN
  //   HEXADECIMAL DISPLAY
endmodule

module multiplier (
  input  in_1,
  input  in_2,
  input  in_3,
  input  in_4,
  input  in_5,
  input  in_6,
  input  in_7,
  input  in_8,
  input  in_9,
  input  in_10,
  input  in_11,
  input  in_12,
  input  in_13,
  input  in_14,
  input  in_15,
  input  in_16,
  output out_17,
  output out_18,
  output out_19,
  output out_20,
  output out_21,
  output out_22,
  output out_23,
  output out_24,
  output out_25,
  output out_26,
  output out_27,
  output out_28,
  output out_29,
  output out_30,
  output out_31,
  output out_32
);

  wire adder_subtractor_1_s1, adder_subtractor_1_s2, adder_subtractor_1_s3, adder_subtractor_1_s4,
       adder_subtractor_1_s5, adder_subtractor_1_s6, adder_subtractor_1_s7, adder_subtractor_1_sign,
       adder_subtractor_2_s1, adder_subtractor_2_s2, adder_subtractor_2_s3, adder_subtractor_2_s4,
       adder_subtractor_2_s5, adder_subtractor_2_s6, adder_subtractor_2_s7, adder_subtractor_2_sign,
       adder_subtractor_3_s1, adder_subtractor_3_s2, adder_subtractor_3_s3, adder_subtractor_3_s4,
       adder_subtractor_3_s5, adder_subtractor_3_s6, adder_subtractor_3_s7, adder_subtractor_3_sign,
       adder_subtractor_4_s1, adder_subtractor_4_s2, adder_subtractor_4_s3, adder_subtractor_4_s4,
       adder_subtractor_4_s5, adder_subtractor_4_s6, adder_subtractor_4_s7, adder_subtractor_4_sign,
       adder_subtractor_5_s1, adder_subtractor_5_s2, adder_subtractor_5_s3, adder_subtractor_5_s4,
       adder_subtractor_5_s5, adder_subtractor_5_s6, adder_subtractor_5_s7, adder_subtractor_5_sign,
       adder_subtractor_7_s1, adder_subtractor_7_s2, adder_subtractor_7_s3, adder_subtractor_7_s4,
       adder_subtractor_7_s5, adder_subtractor_7_s6, adder_subtractor_7_s7, adder_subtractor_7_sign,
       and_helper_1_out_10, and_helper_1_out_11, and_helper_1_out_12, and_helper_1_out_13,
       and_helper_1_out_14, and_helper_1_out_15, and_helper_1_out_16, and_helper_1_out_17,
       and_helper_2_out_10, and_helper_2_out_11, and_helper_2_out_12, and_helper_2_out_13,
       and_helper_2_out_14, and_helper_2_out_15, and_helper_2_out_16, and_helper_2_out_17,
       and_helper_3_out_11, and_helper_3_out_12, and_helper_3_out_13, and_helper_3_out_14,
       and_helper_3_out_15, and_helper_3_out_16, and_helper_3_out_17, and_helper_4_out_10,
       and_helper_4_out_11, and_helper_4_out_12, and_helper_4_out_13, and_helper_4_out_14,
       and_helper_4_out_15, and_helper_4_out_16, and_helper_4_out_17, and_helper_5_out_10,
       and_helper_5_out_11, and_helper_5_out_12, and_helper_5_out_13, and_helper_5_out_14,
       and_helper_5_out_15, and_helper_5_out_16, and_helper_5_out_17, and_helper_6_out_10,
       and_helper_6_out_11, and_helper_6_out_12, and_helper_6_out_13, and_helper_6_out_14,
       and_helper_6_out_15, and_helper_6_out_16, and_helper_6_out_17, and_helper_7_out_10,
       and_helper_7_out_11, and_helper_7_out_12, and_helper_7_out_13, and_helper_7_out_14,
       and_helper_7_out_15, and_helper_7_out_16, and_helper_7_out_17, and_helper_8_out_10,
       and_helper_8_out_11, and_helper_8_out_12, and_helper_8_out_13, and_helper_8_out_14,
       and_helper_8_out_15, and_helper_8_out_16, and_helper_8_out_17;

  And_helper and_helper_1 (
    .in_1(in_8), .in_2(in_7), .in_3(in_6), .in_4(in_5), .in_5(in_4), .in_6(in_3), .in_7(in_2), .in_8(in_1),
    .in_9(in_12), .out_10(and_helper_1_out_10), .out_11(and_helper_1_out_11), .out_12(and_helper_1_out_12),
    .out_13(and_helper_1_out_13), .out_14(and_helper_1_out_14), .out_15(and_helper_1_out_15),
    .out_16(and_helper_1_out_16), .out_17(and_helper_1_out_17));
  And_helper and_helper_2 (
    .in_1(in_8), .in_2(in_7), .in_3(in_6), .in_4(in_5), .in_5(in_4), .in_6(in_3), .in_7(in_2), .in_8(in_1),
    .in_9(in_15), .out_10(and_helper_2_out_10), .out_11(and_helper_2_out_11), .out_12(and_helper_2_out_12),
    .out_13(and_helper_2_out_13), .out_14(and_helper_2_out_14), .out_15(and_helper_2_out_15),
    .out_16(and_helper_2_out_16), .out_17(and_helper_2_out_17));
  adder_subtractor adder_subtractor_1 (
    .A7(and_helper_1_out_17), .A6(and_helper_1_out_16), .A5(and_helper_1_out_15), .A4(and_helper_1_out_14),
    .A3(and_helper_1_out_13), .A2(and_helper_1_out_12), .A1(and_helper_1_out_11), .A0(and_helper_1_out_10),
    .B7(adder_subtractor_7_sign), .B6(adder_subtractor_7_s7), .B5(adder_subtractor_7_s6),
    .B4(adder_subtractor_7_s5), .B3(adder_subtractor_7_s4), .B2(adder_subtractor_7_s3),
    .B1(adder_subtractor_7_s2), .B0(adder_subtractor_7_s1), .M(1'b0), .S0(out_19),
    .S1(adder_subtractor_1_s1), .S2(adder_subtractor_1_s2), .S3(adder_subtractor_1_s3),
    .S4(adder_subtractor_1_s4), .S5(adder_subtractor_1_s5), .S6(adder_subtractor_1_s6),
    .S7(adder_subtractor_1_s7), .Sign(adder_subtractor_1_sign));  // open: V
  And_helper and_helper_3 (
    .in_1(in_8), .in_2(in_7), .in_3(in_6), .in_4(in_5), .in_5(in_4), .in_6(in_3), .in_7(in_2), .in_8(in_1),
    .in_9(in_16), .out_10(out_23), .out_11(and_helper_3_out_11), .out_12(and_helper_3_out_12),
    .out_13(and_helper_3_out_13), .out_14(and_helper_3_out_14), .out_15(and_helper_3_out_15),
    .out_16(and_helper_3_out_16), .out_17(and_helper_3_out_17));
  And_helper and_helper_4 (
    .in_1(in_8), .in_2(in_7), .in_3(in_6), .in_4(in_5), .in_5(in_4), .in_6(in_3), .in_7(in_2), .in_8(in_1),
    .in_9(in_11), .out_10(and_helper_4_out_10), .out_11(and_helper_4_out_11), .out_12(and_helper_4_out_12),
    .out_13(and_helper_4_out_13), .out_14(and_helper_4_out_14), .out_15(and_helper_4_out_15),
    .out_16(and_helper_4_out_16), .out_17(and_helper_4_out_17));
  adder_subtractor adder_subtractor_2 (
    .A7(and_helper_4_out_17), .A6(and_helper_4_out_16), .A5(and_helper_4_out_15), .A4(and_helper_4_out_14),
    .A3(and_helper_4_out_13), .A2(and_helper_4_out_12), .A1(and_helper_4_out_11), .A0(and_helper_4_out_10),
    .B7(adder_subtractor_1_sign), .B6(adder_subtractor_1_s7), .B5(adder_subtractor_1_s6),
    .B4(adder_subtractor_1_s5), .B3(adder_subtractor_1_s4), .B2(adder_subtractor_1_s3),
    .B1(adder_subtractor_1_s2), .B0(adder_subtractor_1_s1), .M(1'b0), .S0(out_18),
    .S1(adder_subtractor_2_s1), .S2(adder_subtractor_2_s2), .S3(adder_subtractor_2_s3),
    .S4(adder_subtractor_2_s4), .S5(adder_subtractor_2_s5), .S6(adder_subtractor_2_s6),
    .S7(adder_subtractor_2_s7), .Sign(adder_subtractor_2_sign));  // open: V
  adder_subtractor adder_subtractor_3 (
    .A7(and_helper_2_out_17), .A6(and_helper_2_out_16), .A5(and_helper_2_out_15), .A4(and_helper_2_out_14),
    .A3(and_helper_2_out_13), .A2(and_helper_2_out_12), .A1(and_helper_2_out_11), .A0(and_helper_2_out_10),
    .B7(1'b0), .B6(and_helper_3_out_17), .B5(and_helper_3_out_16), .B4(and_helper_3_out_15),
    .B3(and_helper_3_out_14), .B2(and_helper_3_out_13), .B1(and_helper_3_out_12), .B0(and_helper_3_out_11),
    .M(1'b0), .S0(out_22), .S1(adder_subtractor_3_s1), .S2(adder_subtractor_3_s2),
    .S3(adder_subtractor_3_s3), .S4(adder_subtractor_3_s4), .S5(adder_subtractor_3_s5),
    .S6(adder_subtractor_3_s6), .S7(adder_subtractor_3_s7), .Sign(adder_subtractor_3_sign));  // open: V
  And_helper and_helper_5 (
    .in_1(in_8), .in_2(in_7), .in_3(in_6), .in_4(in_5), .in_5(in_4), .in_6(in_3), .in_7(in_2), .in_8(in_1),
    .in_9(in_10), .out_10(and_helper_5_out_10), .out_11(and_helper_5_out_11), .out_12(and_helper_5_out_12),
    .out_13(and_helper_5_out_13), .out_14(and_helper_5_out_14), .out_15(and_helper_5_out_15),
    .out_16(and_helper_5_out_16), .out_17(and_helper_5_out_17));
  adder_subtractor adder_subtractor_4 (
    .A7(and_helper_5_out_17), .A6(and_helper_5_out_16), .A5(and_helper_5_out_15), .A4(and_helper_5_out_14),
    .A3(and_helper_5_out_13), .A2(and_helper_5_out_12), .A1(and_helper_5_out_11), .A0(and_helper_5_out_10),
    .B7(adder_subtractor_2_sign), .B6(adder_subtractor_2_s7), .B5(adder_subtractor_2_s6),
    .B4(adder_subtractor_2_s5), .B3(adder_subtractor_2_s4), .B2(adder_subtractor_2_s3),
    .B1(adder_subtractor_2_s2), .B0(adder_subtractor_2_s1), .M(1'b0), .S0(out_17),
    .S1(adder_subtractor_4_s1), .S2(adder_subtractor_4_s2), .S3(adder_subtractor_4_s3),
    .S4(adder_subtractor_4_s4), .S5(adder_subtractor_4_s5), .S6(adder_subtractor_4_s6),
    .S7(adder_subtractor_4_s7), .Sign(adder_subtractor_4_sign));  // open: V
  And_helper and_helper_6 (
    .in_1(in_8), .in_2(in_7), .in_3(in_6), .in_4(in_5), .in_5(in_4), .in_6(in_3), .in_7(in_2), .in_8(in_1),
    .in_9(in_14), .out_10(and_helper_6_out_10), .out_11(and_helper_6_out_11), .out_12(and_helper_6_out_12),
    .out_13(and_helper_6_out_13), .out_14(and_helper_6_out_14), .out_15(and_helper_6_out_15),
    .out_16(and_helper_6_out_16), .out_17(and_helper_6_out_17));
  And_helper and_helper_7 (
    .in_1(in_8), .in_2(in_7), .in_3(in_6), .in_4(in_5), .in_5(in_4), .in_6(in_3), .in_7(in_2), .in_8(in_1),
    .in_9(in_9), .out_10(and_helper_7_out_10), .out_11(and_helper_7_out_11), .out_12(and_helper_7_out_12),
    .out_13(and_helper_7_out_13), .out_14(and_helper_7_out_14), .out_15(and_helper_7_out_15),
    .out_16(and_helper_7_out_16), .out_17(and_helper_7_out_17));
  adder_subtractor adder_subtractor_5 (
    .A7(and_helper_6_out_17), .A6(and_helper_6_out_16), .A5(and_helper_6_out_15), .A4(and_helper_6_out_14),
    .A3(and_helper_6_out_13), .A2(and_helper_6_out_12), .A1(and_helper_6_out_11), .A0(and_helper_6_out_10),
    .B7(adder_subtractor_3_sign), .B6(adder_subtractor_3_s7), .B5(adder_subtractor_3_s6),
    .B4(adder_subtractor_3_s5), .B3(adder_subtractor_3_s4), .B2(adder_subtractor_3_s3),
    .B1(adder_subtractor_3_s2), .B0(adder_subtractor_3_s1), .M(1'b0), .S0(out_21),
    .S1(adder_subtractor_5_s1), .S2(adder_subtractor_5_s2), .S3(adder_subtractor_5_s3),
    .S4(adder_subtractor_5_s4), .S5(adder_subtractor_5_s5), .S6(adder_subtractor_5_s6),
    .S7(adder_subtractor_5_s7), .Sign(adder_subtractor_5_sign));  // open: V
  And_helper and_helper_8 (
    .in_1(in_8), .in_2(in_7), .in_3(in_6), .in_4(in_5), .in_5(in_4), .in_6(in_3), .in_7(in_2), .in_8(in_1),
    .in_9(in_13), .out_10(and_helper_8_out_10), .out_11(and_helper_8_out_11), .out_12(and_helper_8_out_12),
    .out_13(and_helper_8_out_13), .out_14(and_helper_8_out_14), .out_15(and_helper_8_out_15),
    .out_16(and_helper_8_out_16), .out_17(and_helper_8_out_17));
  adder_subtractor adder_subtractor_6 (
    .A7(and_helper_7_out_17), .A6(and_helper_7_out_16), .A5(and_helper_7_out_15), .A4(and_helper_7_out_14),
    .A3(and_helper_7_out_13), .A2(and_helper_7_out_12), .A1(and_helper_7_out_11), .A0(and_helper_7_out_10),
    .B7(adder_subtractor_4_sign), .B6(adder_subtractor_4_s7), .B5(adder_subtractor_4_s6),
    .B4(adder_subtractor_4_s5), .B3(adder_subtractor_4_s4), .B2(adder_subtractor_4_s3),
    .B1(adder_subtractor_4_s2), .B0(adder_subtractor_4_s1), .M(1'b0), .S0(out_32), .S1(out_31), .S2(out_30),
    .S3(out_29), .S4(out_28), .S5(out_27), .S6(out_26), .S7(out_25), .Sign(out_24));  // open: V
  adder_subtractor adder_subtractor_7 (
    .A7(and_helper_8_out_17), .A6(and_helper_8_out_16), .A5(and_helper_8_out_15), .A4(and_helper_8_out_14),
    .A3(and_helper_8_out_13), .A2(and_helper_8_out_12), .A1(and_helper_8_out_11), .A0(and_helper_8_out_10),
    .B7(adder_subtractor_5_sign), .B6(adder_subtractor_5_s7), .B5(adder_subtractor_5_s6),
    .B4(adder_subtractor_5_s5), .B3(adder_subtractor_5_s4), .B2(adder_subtractor_5_s3),
    .B1(adder_subtractor_5_s2), .B0(adder_subtractor_5_s1), .M(1'b0), .S0(out_20),
    .S1(adder_subtractor_7_s1), .S2(adder_subtractor_7_s2), .S3(adder_subtractor_7_s3),
    .S4(adder_subtractor_7_s4), .S5(adder_subtractor_7_s5), .S6(adder_subtractor_7_s6),
    .S7(adder_subtractor_7_s7), .Sign(adder_subtractor_7_sign));  // open: V

  // Other names for the same wires on the sheet: A0 = in_8; A1 = in_7; A2 = in_6; A3 = in_5; A4 = in_4; A5 = in_3;
  //   A6 = in_2; A7 = in_1; B0 = in_16; B1 = in_15; B2 = in_14; B3 = in_13; B4 = in_12; B5 = in_11; B6 = in_10;
  //   B7 = in_9
endmodule

module adder_subtractor (
  input  A7,
  input  A6,
  input  A5,
  input  A4,
  input  A3,
  input  A2,
  input  A1,
  input  A0,
  input  B7,
  input  B6,
  input  B5,
  input  B4,
  input  B3,
  input  B2,
  input  B1,
  input  B0,
  input  M,
  output S0,
  output S1,
  output S2,
  output S3,
  output S4,
  output S5,
  output S6,
  output S7,
  output V,
  output Sign
);

  wire and_1_out, and_2_out, and_3_out, and_4_out, and_5_out, and_6_out, and_7_out, and_8_out, and_9_out,
       and_10_out, and_11_out, and_12_out, and_13_out, and_14_out, and_15_out, and_16_out, and_17_out,
       and_18_out, and_19_out, and_20_out, and_21_out, and_22_out, and_23_out, and_24_out, and_25_out,
       and_26_out, and_27_out, and_28_out, and_29_out, and_30_out, and_31_out, and_32_out, and_33_out,
       and_34_out, and_35_out, and_36_out, and_37_out, and_38_out, or_1_out, or_2_out, or_3_out, or_4_out,
       or_5_out, or_6_out, or_7_out, or_8_out, or_9_out, or_10_out, or_11_out, or_12_out, xor_1_out,
       xor_2_out, xor_3_out, xor_4_out, xor_5_out, xor_6_out, xor_7_out, xor_8_out, xor_9_out, xor_10_out,
       xor_11_out, xor_12_out, xor_13_out, xor_14_out, xor_15_out, xor_16_out, xor_17_out, xor_18_out,
       xor_19_out, xor_20_out, xor_21_out, xor_22_out, xor_23_out, xor_24_out, xor_26_out, xor_28_out;

  xor xor_1 (xor_1_out, or_3_out, or_1_out);
  xor xor_2 (xor_2_out, or_4_out, or_2_out);
  Multiplexer multiplexer_1 (.in0(xor_1_out), .in1(xor_2_out), .out(V), .sel(or_9_out), .en(1'b1));
  Multiplexer multiplexer_2 (.in0(or_1_out), .in1(or_2_out), .out(Sign), .sel(or_9_out), .en(1'b1));
  xor xor_3 (xor_3_out, B6, M);
  xor xor_4 (xor_4_out, B7, M);
  xor xor_5 (xor_5_out, B5, M);
  and and_1 (and_1_out, A7, xor_4_out);
  xor xor_6 (xor_6_out, A7, xor_4_out);
  and and_2 (and_2_out, 1'b0, xor_6_out, xor_18_out, xor_15_out, xor_12_out);
  or or_1 (or_1_out, and_1_out, and_2_out, and_4_out, and_6_out, and_7_out);
  and and_3 (and_3_out, 1'b1, xor_6_out, xor_18_out, xor_15_out, xor_12_out);
  or or_2 (or_2_out, and_1_out, and_3_out, and_5_out, and_8_out, and_9_out);
  xor xor_7 (xor_7_out, B4, M);
  xor xor_8 (xor_8_out, B3, M);
  and and_4 (and_4_out, and_22_out, xor_15_out, xor_6_out, xor_12_out);
  and and_5 (and_5_out, and_22_out, xor_15_out, xor_6_out, xor_12_out);
  xor xor_9 (xor_9_out, B1, M);
  xor xor_10 (xor_10_out, B2, M);
  and and_6 (and_6_out, and_15_out, xor_6_out, xor_12_out);
  and and_7 (and_7_out, and_10_out, xor_6_out);
  and and_8 (and_8_out, and_15_out, xor_6_out, xor_12_out);
  and and_9 (and_9_out, and_10_out, xor_6_out);
  xor xor_11 (xor_11_out, B0, M);
  and and_10 (and_10_out, A6, xor_3_out);
  or or_3 (or_3_out, and_10_out, and_11_out, and_12_out, and_16_out);
  or or_4 (or_4_out, and_10_out, and_14_out, and_13_out, and_17_out);
  xor xor_12 (xor_12_out, A6, xor_3_out);
  and and_11 (and_11_out, 1'b0, xor_12_out, xor_18_out, xor_15_out);
  and and_12 (and_12_out, xor_12_out, xor_15_out, and_22_out);
  xor xor_13 (xor_13_out, or_3_out, xor_6_out);
  and and_13 (and_13_out, xor_12_out, xor_15_out, and_22_out);
  and and_14 (and_14_out, 1'b1, xor_12_out, xor_18_out, xor_15_out);
  xor xor_14 (xor_14_out, or_4_out, xor_6_out);
  and and_15 (and_15_out, A5, xor_5_out);
  and and_16 (and_16_out, xor_12_out, and_15_out);
  and and_17 (and_17_out, xor_12_out, and_15_out);
  or or_5 (or_5_out, and_15_out, and_20_out, and_21_out);
  xor xor_15 (xor_15_out, A5, xor_5_out);
  and and_18 (and_18_out, 1'b0, xor_15_out, xor_18_out);
  and and_19 (and_19_out, xor_15_out, and_22_out);
  or or_6 (or_6_out, and_15_out, and_18_out, and_19_out);
  xor xor_16 (xor_16_out, or_6_out, xor_12_out);
  and and_20 (and_20_out, 1'b1, xor_15_out, xor_18_out);
  and and_21 (and_21_out, xor_15_out, and_22_out);
  xor xor_17 (xor_17_out, or_5_out, xor_12_out);
  and and_22 (and_22_out, A4, xor_7_out);
  or or_7 (or_7_out, and_22_out, and_23_out);
  or or_8 (or_8_out, and_22_out, and_24_out);
  xor xor_18 (xor_18_out, A4, xor_7_out);
  and and_23 (and_23_out, xor_18_out, 1'b0);
  xor xor_19 (xor_19_out, or_7_out, xor_15_out);
  and and_24 (and_24_out, xor_18_out, 1'b1);
  xor xor_20 (xor_20_out, or_8_out, xor_15_out);
  xor xor_21 (xor_21_out, xor_18_out, 1'b0);
  xor xor_22 (xor_22_out, xor_18_out, 1'b1);
  xor xor_23 (xor_23_out, A3, xor_8_out);
  and and_25 (and_25_out, A3, xor_8_out);
  and and_26 (and_26_out, M, xor_23_out, xor_28_out, xor_26_out, xor_24_out);
  or or_9 (or_9_out, and_25_out, and_26_out, and_27_out, and_29_out, and_28_out);
  Multiplexer multiplexer_3 (.in0(xor_21_out), .in1(xor_22_out), .out(S4), .sel(or_9_out), .en(1'b1));
  Multiplexer multiplexer_4 (.in0(xor_19_out), .in1(xor_20_out), .out(S5), .sel(or_9_out), .en(1'b1));
  Multiplexer multiplexer_5 (.in0(xor_16_out), .in1(xor_17_out), .out(S6), .sel(or_9_out), .en(1'b1));
  Multiplexer multiplexer_6 (.in0(xor_13_out), .in1(xor_14_out), .out(S7), .sel(or_9_out), .en(1'b1));
  and and_27 (and_27_out, and_36_out, xor_26_out, xor_23_out, xor_24_out);
  and and_28 (and_28_out, and_30_out, xor_23_out);
  and and_29 (and_29_out, and_34_out, xor_23_out, xor_24_out);
  and and_30 (and_30_out, A2, xor_10_out);
  xor xor_24 (xor_24_out, A2, xor_10_out);
  and and_31 (and_31_out, M, xor_24_out, xor_28_out, xor_26_out);
  or or_10 (or_10_out, and_30_out, and_31_out, and_33_out, and_32_out);
  xor xor_25 (S3, or_10_out, xor_23_out);
  and and_32 (and_32_out, xor_24_out, and_34_out);
  and and_33 (and_33_out, xor_24_out, xor_26_out, and_36_out);
  xor xor_26 (xor_26_out, A1, xor_9_out);
  and and_34 (and_34_out, A1, xor_9_out);
  and and_35 (and_35_out, M, xor_26_out, xor_28_out);
  or or_11 (or_11_out, and_34_out, and_35_out, and_37_out);
  xor xor_27 (S2, or_11_out, xor_24_out);
  and and_36 (and_36_out, A0, xor_11_out);
  and and_37 (and_37_out, xor_26_out, and_36_out);
  or or_12 (or_12_out, and_36_out, and_38_out);
  xor xor_28 (xor_28_out, A0, xor_11_out);
  and and_38 (and_38_out, xor_28_out, M);
  xor xor_29 (S1, or_12_out, xor_26_out);
  xor xor_30 (S0, xor_28_out, M);
endmodule

module And_helper (
  input  in_1,
  input  in_2,
  input  in_3,
  input  in_4,
  input  in_5,
  input  in_6,
  input  in_7,
  input  in_8,
  input  in_9,
  output out_10,
  output out_11,
  output out_12,
  output out_13,
  output out_14,
  output out_15,
  output out_16,
  output out_17
);

  and and_1 (out_10, in_1, in_9);
  and and_2 (out_11, in_2, in_9);
  and and_3 (out_12, in_3, in_9);
  and and_4 (out_13, in_4, in_9);
  and and_5 (out_14, in_5, in_9);
  and and_6 (out_15, in_6, in_9);
  and and_7 (out_16, in_7, in_9);
  and and_8 (out_17, in_8, in_9);
endmodule

module _7segdisplay (
  input  A,
  input  B,
  input  C,
  input  D,
  output out_5,
  output out_6,
  output out_7,
  output out_8,
  output out_9,
  output out_10,
  output out_11
);

  wire and_1_out, and_2_out, and_3_out, and_4_out, and_5_out, and_6_out, and_7_out, and_8_out, and_9_out,
       and_10_out, and_11_out, and_12_out, and_13_out, and_14_out, and_15_out, and_16_out, and_17_out,
       and_18_out, and_19_out, and_20_out, and_21_out, and_22_out, and_23_out, and_24_out, and_25_out,
       and_26_out, and_27_out, and_28_out, and_29_out, and_30_out, and_31_out, and_32_out, and_33_out,
       and_34_out, and_35_out, not_1_out, not_2_out, not_3_out, not_4_out;

  not not_1 (not_1_out, A);
  not not_2 (not_2_out, B);
  not not_3 (not_3_out, C);
  not not_4 (not_4_out, D);
  and and_1 (and_1_out, not_2_out, not_4_out);
  and and_2 (and_2_out, not_1_out, not_2_out);
  and and_3 (and_3_out, A, not_3_out, D);
  and and_4 (and_4_out, not_1_out, C, D);
  and and_5 (and_5_out, not_4_out, not_3_out, not_1_out);
  and and_6 (and_6_out, A, not_2_out);
  and and_7 (and_7_out, not_1_out, B);
  and and_8 (and_8_out, not_3_out, D);
  and and_9 (and_9_out, not_1_out, not_3_out);
  and and_10 (and_10_out, not_1_out, D);
  and and_11 (and_11_out, A, not_3_out);
  and and_12 (and_12_out, B, not_3_out, D);
  and and_13 (and_13_out, not_2_out, C, D);
  and and_14 (and_14_out, not_4_out, not_2_out, not_1_out);
  and and_15 (and_15_out, not_4_out, C, B);
  and and_16 (and_16_out, C, not_4_out);
  and and_17 (and_17_out, A, B);
  and and_18 (and_18_out, A, C);
  and and_19 (and_19_out, not_2_out, not_4_out);
  and and_20 (and_20_out, A, not_2_out);
  and and_21 (and_21_out, not_3_out, not_4_out);
  and and_22 (and_22_out, A, C);
  and and_23 (and_23_out, not_1_out, B, not_3_out);
  and and_24 (and_24_out, B, C, not_4_out);
  and and_25 (and_25_out, not_4_out, not_2_out);
  and and_26 (and_26_out, not_1_out, C);
  and and_27 (and_27_out, A, not_4_out);
  and and_28 (and_28_out, C, B);
  and and_29 (and_29_out, not_1_out, D, B);
  and and_30 (and_30_out, A, not_2_out, not_3_out);
  and and_31 (and_31_out, C, not_4_out);
  and and_32 (and_32_out, A, D);
  and and_33 (and_33_out, A, not_2_out);
  and and_34 (and_34_out, not_2_out, not_1_out, C);
  and and_35 (and_35_out, not_3_out, B, not_1_out);
  or e (out_9, and_20_out, and_21_out, and_22_out, and_23_out, and_24_out);
  or u_a (out_5, and_1_out, and_2_out, and_3_out, and_4_out, and_5_out);
  or u_b (out_6, and_6_out, and_7_out, and_8_out, and_9_out, and_10_out);
  or u_c (out_7, and_11_out, and_12_out, and_13_out, and_14_out, and_15_out);
  or u_d (out_8, and_16_out, and_17_out, and_18_out, and_19_out);
  or f (out_10, and_25_out, and_26_out, and_27_out, and_28_out, and_29_out, and_30_out);
  or g (out_11, and_31_out, and_32_out, and_33_out, and_34_out, and_35_out);
endmodule

module Divider (
  input  in_1,
  input  in_2,
  input  in_3,
  input  in_4,
  input  in_5,
  input  in_6,
  input  in_7,
  input  in_8,
  input  in_9,
  input  in_10,
  input  in_11,
  input  in_12,
  input  in_13,
  input  in_14,
  input  in_15,
  input  in_16,
  output out_17,
  output out_18,
  output out_19,
  output out_20,
  output out_21,
  output out_22,
  output out_23,
  output out_24,
  output out_25,
  output out_26,
  output out_27,
  output out_28,
  output out_29,
  output out_30,
  output out_31,
  output out_32
);

  wire _00, _01, _02, _03, _04, _05, _06, _07, _10, _11, _12, _13, _14, _15, _16, _17, _20, _21, _22, _23,
       _24, _25, _26, _27, _30, _31, _32, _33, _34, _35, _36, _37, _40, _41, _42, _43, _44, _45, _46, _47,
       _50, _51, _52, _53, _54, _55, _56, _57, _60, _61, _62, _63, _64, _65, _66, _67;

  Division_sub division_sub_1 (
    .in_1(1'b0), .in_2(1'b0), .in_3(in_1), .in_4(1'b0), .in_5(in_2), .in_6(1'b0), .in_7(in_3), .in_8(1'b0),
    .in_9(in_4), .in_10(1'b0), .in_11(in_5), .in_12(1'b0), .in_13(in_6), .in_14(in_9), .in_15(in_7),
    .in_16(in_8), .out_17(out_17), .out_18(_07), .out_19(_06), .out_20(_05), .out_21(_04), .out_22(_03),
    .out_23(_02), .out_24(_01), .out_25(_00));
  Division_sub division_sub_2 (
    .in_1(_06), .in_2(_05), .in_3(in_1), .in_4(_04), .in_5(in_2), .in_6(_03), .in_7(in_3), .in_8(_02),
    .in_9(in_4), .in_10(_01), .in_11(in_5), .in_12(_00), .in_13(in_6), .in_14(in_10), .in_15(in_7),
    .in_16(in_8), .out_17(out_18), .out_18(_17), .out_19(_16), .out_20(_15), .out_21(_14), .out_22(_13),
    .out_23(_12), .out_24(_11), .out_25(_10));
  Division_sub division_sub_3 (
    .in_1(_16), .in_2(_15), .in_3(in_1), .in_4(_14), .in_5(in_2), .in_6(_13), .in_7(in_3), .in_8(_12),
    .in_9(in_4), .in_10(_11), .in_11(in_5), .in_12(_10), .in_13(in_6), .in_14(in_11), .in_15(in_7),
    .in_16(in_8), .out_17(out_19), .out_18(_27), .out_19(_26), .out_20(_25), .out_21(_24), .out_22(_23),
    .out_23(_22), .out_24(_21), .out_25(_20));
  Division_sub division_sub_4 (
    .in_1(_26), .in_2(_25), .in_3(in_1), .in_4(_24), .in_5(in_2), .in_6(_23), .in_7(in_3), .in_8(_22),
    .in_9(in_4), .in_10(_21), .in_11(in_5), .in_12(_20), .in_13(in_6), .in_14(in_12), .in_15(in_7),
    .in_16(in_8), .out_17(out_20), .out_18(_37), .out_19(_36), .out_20(_35), .out_21(_34), .out_22(_33),
    .out_23(_32), .out_24(_31), .out_25(_30));
  Division_sub division_sub_5 (
    .in_1(_36), .in_2(_35), .in_3(in_1), .in_4(_34), .in_5(in_2), .in_6(_33), .in_7(in_3), .in_8(_32),
    .in_9(in_4), .in_10(_31), .in_11(in_5), .in_12(_30), .in_13(in_6), .in_14(in_13), .in_15(in_7),
    .in_16(in_8), .out_17(out_21), .out_18(_47), .out_19(_46), .out_20(_45), .out_21(_44), .out_22(_43),
    .out_23(_42), .out_24(_41), .out_25(_40));
  Division_sub division_sub_6 (
    .in_1(_46), .in_2(_45), .in_3(in_1), .in_4(_44), .in_5(in_2), .in_6(_43), .in_7(in_3), .in_8(_42),
    .in_9(in_4), .in_10(_41), .in_11(in_5), .in_12(_40), .in_13(in_6), .in_14(in_14), .in_15(in_7),
    .in_16(in_8), .out_17(out_22), .out_18(_57), .out_19(_56), .out_20(_55), .out_21(_54), .out_22(_53),
    .out_23(_52), .out_24(_51), .out_25(_50));
  Division_sub division_sub_7 (
    .in_1(_56), .in_2(_55), .in_3(in_1), .in_4(_54), .in_5(in_2), .in_6(_53), .in_7(in_3), .in_8(_52),
    .in_9(in_4), .in_10(_51), .in_11(in_5), .in_12(_50), .in_13(in_6), .in_14(in_15), .in_15(in_7),
    .in_16(in_8), .out_17(out_23), .out_18(_67), .out_19(_66), .out_20(_65), .out_21(_64), .out_22(_63),
    .out_23(_62), .out_24(_61), .out_25(_60));
  Division_sub division_sub_8 (
    .in_1(_66), .in_2(_65), .in_3(in_1), .in_4(_64), .in_5(in_2), .in_6(_63), .in_7(in_3), .in_8(_62),
    .in_9(in_4), .in_10(_61), .in_11(in_5), .in_12(_60), .in_13(in_6), .in_14(in_16), .in_15(in_7),
    .in_16(in_8), .out_17(out_24), .out_18(out_25), .out_19(out_26), .out_20(out_27), .out_21(out_28),
    .out_22(out_29), .out_23(out_30), .out_24(out_31), .out_25(out_32));

  // Other names for the same wires on the sheet: D0 = in_16; d0_t = in_8; D1 = in_15; d1_t = in_7; D2 = in_14;
  //   d2_t = in_6; D3 = in_13; d3_t = in_5; D4 = in_12; d4_t = in_4; D5 = in_11; d5_t = in_3; D6 = in_10; d6_t = in_2;
  //   D7 = in_9; d7_t = in_1; Q0 = out_24; Q1 = out_23; Q2 = out_22; Q3 = out_21; Q4 = out_20; Q5 = out_19;
  //   Q6 = out_18; Q7 = out_17; R0 = out_32; R1 = out_31; R2 = out_30; R3 = out_29; R4 = out_28; R5 = out_27;
  //   R6 = out_26; R7 = out_25
endmodule

module Shift_to_down (
  input  in_1,
  input  in_2,
  input  in_3,
  input  in_4,
  input  in_5,
  input  in_6,
  input  in_7,
  input  in_8,
  input  in_9,
  input  in_10,
  input  in_11,
  input  in_12,
  input  in_13,
  input  in_14,
  input  in_15,
  input  in_16,
  input  in_17,
  input  in_18,
  output out_19,
  output out_20,
  output out_21,
  output out_22,
  output out_23,
  output out_24,
  output out_25,
  output out_26
);

  Multiplexer multiplexer_1 (.in0(in_9), .in1(in_1), .out(out_19), .sel(in_17), .en(in_18));
  Multiplexer multiplexer_2 (.in0(in_10), .in1(in_2), .out(out_20), .sel(in_17), .en(in_18));
  Multiplexer multiplexer_3 (.in0(in_11), .in1(in_3), .out(out_21), .sel(in_17), .en(in_18));
  Multiplexer multiplexer_4 (.in0(in_12), .in1(in_4), .out(out_22), .sel(in_17), .en(in_18));
  Multiplexer multiplexer_5 (.in0(in_13), .in1(in_5), .out(out_23), .sel(in_17), .en(in_18));
  Multiplexer multiplexer_6 (.in0(in_15), .in1(in_7), .out(out_25), .sel(in_17), .en(in_18));
  Multiplexer multiplexer_7 (.in0(in_14), .in1(in_6), .out(out_24), .sel(in_17), .en(in_18));
  Multiplexer multiplexer_8 (.in0(in_16), .in1(in_8), .out(out_26), .sel(in_17), .en(in_18));
endmodule

module Division_sub (
  input  in_1,
  input  in_2,
  input  in_3,
  input  in_4,
  input  in_5,
  input  in_6,
  input  in_7,
  input  in_8,
  input  in_9,
  input  in_10,
  input  in_11,
  input  in_12,
  input  in_13,
  input  in_14,
  input  in_15,
  input  in_16,
  output out_17,
  output out_18,
  output out_19,
  output out_20,
  output out_21,
  output out_22,
  output out_23,
  output out_24,
  output out_25
);

  wire adder_subtractor_1_s0, adder_subtractor_1_s1, adder_subtractor_1_s2, adder_subtractor_1_s3,
       adder_subtractor_1_s4, adder_subtractor_1_s5, adder_subtractor_1_s6, adder_subtractor_1_s7;

  Shift_to_down shift_to_down_1 (
    .in_17(out_17), .in_9(in_1), .in_10(in_2), .in_11(in_4), .in_12(in_6), .in_13(in_8), .in_14(in_10),
    .in_15(in_12), .in_16(in_14), .in_1(adder_subtractor_1_s7), .in_2(adder_subtractor_1_s6),
    .in_3(adder_subtractor_1_s5), .in_4(adder_subtractor_1_s4), .in_5(adder_subtractor_1_s3),
    .in_6(adder_subtractor_1_s2), .in_7(adder_subtractor_1_s1), .in_8(adder_subtractor_1_s0),
    .out_19(out_18), .out_20(out_19), .out_21(out_20), .out_22(out_21), .out_23(out_22), .out_24(out_23),
    .out_25(out_24), .out_26(out_25));  // open: in_18
  adder_subtractor adder_subtractor_1 (
    .A7(in_1), .A6(in_2), .A5(in_4), .A4(in_6), .A3(in_8), .A2(in_10), .A1(in_12), .A0(in_14), .B7(in_3),
    .B6(in_5), .B5(in_7), .B4(in_9), .B3(in_11), .B2(in_13), .B1(in_15), .B0(in_16), .M(1'b1),
    .S0(adder_subtractor_1_s0), .S1(adder_subtractor_1_s1), .S2(adder_subtractor_1_s2),
    .S3(adder_subtractor_1_s3), .S4(adder_subtractor_1_s4), .S5(adder_subtractor_1_s5),
    .S6(adder_subtractor_1_s6), .S7(adder_subtractor_1_s7), .Sign(out_17));  // open: V
endmodule
